# Fritzing sketch 01_blinkBlink (saved by Fritzing 0.9.0b)
breadboards: 1

parts:
  LED1 = LED - 5mm [color="Red (633nm)" package="5 mm [THT]"]  # not connected
  R1 = Resistor [tolerance=±10% resistance=220 package=THT]
  Composants1 = Arduino Uno (Rev3)

nets:
  N1: R1.Pin_0, Composants1.D13/SCK
