# Fritzing sketch 02_servoWave (saved by Fritzing 0.8.7b)
breadboards: 1

parts:
  J2 = Basic Servo
  Composants1 = Arduino Uno (Rev3)

nets:
  GND: J2.gnd, Composants1.GND
  VCC: J2.vcc, Composants1.5V
  N1: J2.pulse, Composants1.D9_PWM
