# Fritzing sketch 03_spinMotorSpin (saved by Fritzing 0.8.7b)
breadboards: 1

parts:
  Composants1 = Arduino Uno (Rev3)
  M1 = DC Motor
  Q1 = NPN-Transistor [package="TO92 [THT]"]
  R1 = Resistor [tolerance=±5% resistance=220 package=THT]
  D1 = Diode [package=diode-1n4001]

nets:
  N1: Composants1.D9_PWM, R1.Pin_1
  N2: Composants1.5V, M1.pin_2, D1.A
  N3: Composants1.GND, Q1.E
  N4: M1.pin_1, Q1.C, D1.C
  N5: Q1.B, R1.Pin_0
