# Fritzing sketch 05_lightSwitch (saved by Fritzing 0.8.7b)
breadboards: 1

parts:
  Composants1 = Arduino Uno (Rev3)
  R1 = Resistor [tolerance=±5% resistance=1k package=THT]
  R2 = Resistor [tolerance=±5% resistance=330 package=THT]
  LED1 = LED - 5mm [color="Red (633nm)" package="5 mm [THT]"]
  S1 = Pushbutton [package="[THT]"]
  R3 = Photocell (LDR) [package=THT]  # not connected

nets (from the breadboard view):
  N1: Composants1.D9_PWM, R2.Pin_1
  N2: Composants1.GND, LED1.cathode
  N3: Composants1.D5_PWM, R1.Pin_0, S1.Pin_3, S1.Pin_4
  N4: Composants1.5V, S1.Pin_1, S1.Pin_2
  N5: R2.Pin_0, LED1.anode
