# Fritzing sketch 05_streetLamp (saved by Fritzing 0.9.0b)
breadboards: 1

parts:
  Composants1 = Arduino Uno (Rev3)
  R1 = Resistor [tolerance=±5% resistance=1k package=THT]
  R2 = Resistor [tolerance=±5% resistance=330 package=THT]
  LED1 = LED - 5mm [color="Red (633nm)" package="5 mm [THT]"]
  R3 = PHOTOCELL [package=photocell-kit]

nets:
  N1: Composants1.A0, R1.Pin_0, R3.P$2
  N2: Composants1.D9_PWM, R2.Pin_1
  N3: Composants1.GND, R1.Pin_1, LED1.cathode
  N4: Composants1.5V, R3.P$1
  N5: R2.Pin_0, LED1.anode
