# Fritzing sketch 06_pingBell (saved by Fritzing 0.9.0b)
breadboards: 1

parts:
  Composants1 = Arduino Uno (Rev3)
  J1 = Piezo Speaker

nets:
  N1: Composants1.D9_PWM, J1.pin2
  N2: Composants1.GND, J1.pin1
