# Fritzing sketch 07_robotArm (saved by Fritzing 0.9.0b)
breadboards: 1

parts:
  Composants1 = Arduino Uno (Rev3)
  U1 = POT [package=alps_pot]
  J1 = Basic Servo

nets:
  N1: Composants1.A2, U1.S
  N2: Composants1.D9_PWM, J1.pulse
  GND: Composants1.GND, U1.E, J1.gnd
  5V: Composants1.5V, U1.A, J1.vcc
