# Fritzing sketch 08_remoteTemperature (saved by Fritzing 0.9.0b)
breadboards: 1

parts:
  Composants1 = Arduino Uno (Rev3)
  U1 = TMP36 [package=to-92]

nets:
  N1: Composants1.A0, U1.VOUT
  5V: Composants1.5V, U1.VCC
  GND: Composants1.GND, U1.GND
