# Fritzing sketch 09_fireAlarm (saved by Fritzing 0.9.0b)
breadboards: 1

parts:
  Composants1 = Arduino Uno (Rev3)
  U1 = TMP36 [package=to-92]
  S2 = Pushbutton [package="[THT]"]
  R2 = Resistor [tolerance=±5% resistance=1k package=THT]
  LED2 = LED - 5mm [color="Red (633nm)" package="5 mm [THT]"]
  R3 = Resistor [tolerance=±5% resistance=330 package=THT]
  J1 = Piezo Speaker

nets:
  N1: Composants1.A0, U1.VOUT
  N2: Composants1.D9_PWM, J1.pin2
  N3: Composants1.D13/SCK, R3.Pin_1
  N4: Composants1.D5_PWM, S2.Pin_1, S2.Pin_2, R2.Pin_1
  5V: Composants1.5V, U1.VCC, R2.Pin_0
  GND: Composants1.GND, U1.GND, S2.Pin_3, S2.Pin_4, LED2.cathode, J1.pin1
  N5: LED2.anode, R3.Pin_0
